// Logisim project MazeDriver.circ as structural Verilog: 3 circuits, main circuit main
module main (
  input  reset
);

  wire clock, clock_out, comparator_1_eq, not_1_out, State_Decoder_left, State_Decoder_right;
  wire [1:0] ant_1_action;
  wire [7:0] multiplexer_1_out, ram_1_data, State_Decoder_a0, State_Decoder_a1, State_Decoder_a2;
  wire [31:0] ram_2_data;

  not not_1 (not_1_out, comparator_1_eq);
  Clock u_clock (.out(clock_out));
  and and_1 (clock, not_1_out, clock_out);
  Counter StepsToGoal (.clk(clock), .clr(reset));  // open: load, D, count, Q, carry
  RAM #(.addrWidth(2), .bus("separate")) ram_1 (
    .addr(2'b00), .din(multiplexer_1_out), .data(ram_1_data), .str(1'b1), .sel(1'b1), .clk(clock), .ld(1'b1),
    .clr(reset));
  Comparator comparator_1 (.a(8'h2d), .b(ram_1_data), .eq(comparator_1_eq));  // open: gt, lt
  // Probe on ram_1_data
  LED GOAL (.in(comparator_1_eq));
  RAM #(.dataWidth(32)) ram_2 (.addr(ram_1_data), .data(ram_2_data));  // open: sel, clk, ld, clr
  StateDecoder State_Decoder (
    .in_1(ram_2_data), .Left(State_Decoder_left), .Right(State_Decoder_right), .A0(State_Decoder_a0),
    .A1(State_Decoder_a1), .A2(State_Decoder_a2));
  ant ant_1 (
    .Left(State_Decoder_left), .Right(State_Decoder_right), .clock(clock), .reset(reset),
    .Action(ant_1_action));
  Multiplexer #(.select(2), .width(8)) multiplexer_1 (
    .in0(State_Decoder_a0), .in1(State_Decoder_a1), .in2(State_Decoder_a2), .in3({8{1'b0}}),
    .out(multiplexer_1_out), .sel(ant_1_action));  // open: en
  // Probe on ant_1_action
  // Probe on multiplexer_1_out
endmodule

module AddressMaker (
  input  [7:0] AddressIn,
  output [9:0] AddressOut
);


  assign AddressOut = {AddressIn, 2'b00};
endmodule

module StateDecoder (
  input  [31:0] in_1,
  output Left,
  output Right,
  output [7:0] A0,
  output [7:0] A1,
  output [7:0] A2
);


  assign A0 = in_1[23:16];
  assign A1 = in_1[15:8];
  assign A2 = in_1[7:0];
  assign Left = in_1[28];
  assign Right = in_1[24];
endmodule
