// Logisim project MazeDriver2.circ as structural Verilog: 3 circuits, main circuit main
module main (
  input  reset
);

  wire clock, clock_out, comparator_2_eq, confabulator_1_e, confabulator_1_n, confabulator_1_s,
       confabulator_1_w, not_1_out, not_2_out, SameState, State_Decoder_left, State_Decoder_right;
  wire [1:0] ant_1_action;
  wire [5:0] confabulator_1_col0, confabulator_1_col1, confabulator_1_col2, confabulator_1_col3;
  wire [7:0] multiplexer_1_out, ram_1_data, State_Decoder_a0, State_Decoder_a1, State_Decoder_a2;
  wire [31:0] ram_2_data;

  not not_1 (not_1_out, comparator_2_eq);
  Clock u_clock (.out(clock_out));
  and and_1 (clock, not_1_out, clock_out);
  Counter StepsToGoal (.clk(clock), .clr(reset));  // open: load, D, count, Q, carry
  Counter Collisions (.count(SameState), .clk(clock), .clr(reset));  // open: load, D, Q, carry
  not not_2 (not_2_out, clock);
  Comparator comparator_1 (.a(ram_1_data), .b(multiplexer_1_out), .eq(SameState));  // open: gt, lt
  DotMatrix #(.matrixcols(4), .matrixrows(6)) dotmatrix_1 (
    .col0(confabulator_1_col0), .col1(confabulator_1_col1), .col2(confabulator_1_col2),
    .col3(confabulator_1_col3));
  Confabulator confabulator_1 (
    .in_1(ram_1_data), .Col0(confabulator_1_col0), .Col1(confabulator_1_col1), .Col2(confabulator_1_col2),
    .Col3(confabulator_1_col3), .N(confabulator_1_n), .E(confabulator_1_e), .S(confabulator_1_s),
    .W(confabulator_1_w));
  RAM #(.addrWidth(2), .bus("separate")) ram_1 (
    .addr(2'b00), .din(multiplexer_1_out), .data(ram_1_data), .str(1'b1), .sel(1'b1), .clk(not_2_out),
    .ld(1'b1), .clr(reset));
  LED led_1 (.in(confabulator_1_n));
  LED led_2 (.in(confabulator_1_w));
  LED led_3 (.in(confabulator_1_s));
  Comparator comparator_2 (.a(8'h2d), .b(ram_1_data), .eq(comparator_2_eq));  // open: gt, lt
  // Probe on ram_1_data
  LED led_4 (.in(confabulator_1_e));
  LED GOAL (.in(comparator_2_eq));
  RAM #(.dataWidth(32)) ram_2 (.addr(ram_1_data), .data(ram_2_data));  // open: sel, clk, ld, clr
  StateDecoder State_Decoder (
    .in_1(ram_2_data), .Left(State_Decoder_left), .Right(State_Decoder_right), .A0(State_Decoder_a0),
    .A1(State_Decoder_a1), .A2(State_Decoder_a2));
  ant ant_1 (
    .Left(State_Decoder_left), .Right(State_Decoder_right), .clock(clock), .reset(reset),
    .Action(ant_1_action));
  Multiplexer #(.select(2), .width(8)) multiplexer_1 (
    .in0(State_Decoder_a0), .in1(State_Decoder_a1), .in2(State_Decoder_a2), .in3({8{1'b0}}),
    .out(multiplexer_1_out), .sel(ant_1_action));  // open: en
  // Probe on ant_1_action
  // Probe on multiplexer_1_out
endmodule

module StateDecoder (
  input  [31:0] in_1,
  output Left,
  output Right,
  output [7:0] A0,
  output [7:0] A1,
  output [7:0] A2
);


  assign A0 = in_1[23:16];
  assign A1 = in_1[15:8];
  assign A2 = in_1[7:0];
  assign Left = in_1[28];
  assign Right = in_1[24];
endmodule

module Confabulator (
  input  [7:0] in_1,
  output [5:0] Col0,
  output [5:0] Col1,
  output [5:0] Col2,
  output [5:0] Col3,
  output N,
  output E,
  output S,
  output W
);

  wire [5:0] decoder_1_out5;

  Decoder #(.select(4)) decoder_1 (
    .out0(decoder_1_out5[5]), .out1(decoder_1_out5[4]), .out2(decoder_1_out5[3]), .out3(decoder_1_out5[2]),
    .out4(decoder_1_out5[1]), .out5(decoder_1_out5[0]), .sel(in_1[7:4]));  // open: out6, out7, out8, out9, out10, out11, out12, out13, out14, out15, en
  Demultiplexer #(.select(2), .width(6)) demultiplexer_1 (
    .out0(Col0), .out1(Col1), .out2(Col2), .out3(Col3), .in(decoder_1_out5), .sel(in_1[3:2]));  // open: en
  Demultiplexer #(.select(2)) demultiplexer_2 (
    .out0(N), .out1(E), .out2(S), .out3(W), .in(1'b1), .sel(in_1[1:0]));  // open: en
endmodule
