// Logisim project ant.circ as structural Verilog: 1 circuit, main circuit ant
module ant (
  input  Left,
  input  Right,
  input  clock,
  input  reset,
  output [1:0] Action
);

  wire and_1_out, and_2_out, and_3_out, and_4_out, and_5_out, and_6_out, and_7_out, and_8_out, and_9_out,
       and_10_out, and_11_out, not_1_out, not_2_out, or_1_out, or_2_out, or_3_out, Q0_q, Q0_qn, Q1_q, Q1_qn,
       Q2_q, Q2_qn;

  not not_1 (not_1_out, Left);
  not not_2 (not_2_out, Right);
  and and_1 (and_1_out, Right, Left, Q2_qn);
  and and_2 (and_2_out, Left, not_2_out, Q2_qn, Q0_qn);
  and and_3 (and_3_out, not_2_out, Left, Q1_qn, Q2_qn);
  and and_4 (and_4_out, not_2_out, Q1_q, Q0_qn, Q2_qn);
  and and_5 (and_5_out, Q2_q, Q1_qn, Q0_qn, Right, not_1_out);
  and and_6 (and_6_out, Right, Q0_q, Q1_qn, Q2_qn);
  and and_7 (and_7_out, Q1_q, not_2_out, Q0_qn, Q2_qn);
  and and_8 (and_8_out, Right, Q2_qn, not_1_out);
  and and_9 (and_9_out, Q1_qn, Q0_qn, Q2_q, not_2_out);
  or or_1 (or_1_out, and_4_out, and_9_out, and_8_out, and_3_out);
  and and_10 (and_10_out, not_2_out, Q2_qn, Q1_q, Q0_q);
  or or_2 (or_2_out, and_5_out, and_10_out);
  and and_11 (and_11_out, not_2_out, Q0_qn, Q1_qn, Q2_qn);
  or or_3 (or_3_out, and_1_out, and_6_out, and_2_out, and_7_out, and_11_out);
  D_Flip_Flop Q0 (.clk(clock), .D(or_3_out), .Q(Q0_q), .Qn(Q0_qn), .reset(reset));  // open: preset, en
  D_Flip_Flop Q1 (.clk(clock), .D(or_1_out), .Q(Q1_q), .Qn(Q1_qn), .reset(reset));  // open: preset, en
  D_Flip_Flop Q2 (.clk(clock), .D(or_2_out), .Q(Q2_q), .Qn(Q2_qn), .reset(reset));  // open: preset, en
  and and_12 (Action[1], Q1_q, Q0_q);
  and and_13 (Action[0], Q1_qn, Q0_q);

  // Notes on the sheet:
  //   L
  //   Q0
  //   Q1
  //   R
  //   Q2
endmodule
