// Logisim project ALU.circ as structural Verilog: 2 circuits, main circuit main
module main (
  input  [31:0] aluA,
  input  [31:0] aluB,
  input  [3:0] aluOp,
  input  Cin,
  output CF,
  output ZF,
  output SF,
  output OF,
  output [31:0] valE
);

  ALU32 alu32_1 (.aluA(aluA), .aluB(aluB), .Cin(Cin), .valE(valE), .CF(CF), .ZF(ZF), .SF(SF), .OF(OF), .aluOp(aluOp));
endmodule

module ALU32 (
  input  [31:0] aluA,
  input  [31:0] aluB,
  input  Cin,
  input  [3:0] aluOp,
  output CF,
  output ZF,
  output SF,
  output OF,
  output [31:0] valE
);

  Add32 add32_1 (.A32(aluA), .B32(aluB), .Cin(Cin), .F32(valE), .Cout(CF));

  assign OF = 1'b0;
  assign SF = 1'b0;
  assign ZF = 1'b0;
endmodule
