// Logisim project Y86Control.circ as structural Verilog: 1 circuit, main circuit Y86Control
module Y86Control (
  input  [3:0] icode,
  input  [3:0] ifun,
  input  [2:0] CC,
  input  [1:0] Stat,
  input  imemError,
  input  dmemError,
  output \continue ,
  output statWrite,
  output [1:0] statVal,
  output [1:0] PCIncSrc,
  output valCsrc,
  output valAsrc,
  output valBsrc,
  output aluAsrc,
  output [1:0] aluBsrc,
  output setCC,
  output aluOp,
  output [1:0] dmemAddr,
  output dmemData,
  output dmemWrite,
  output [1:0] dstEsrc,
  output dstMsrc,
  output [1:0] newPC
);

  wire cond_1_cnd;

  \continue  continue_1 (.Stat(Stat), .\continue (\continue ));
  stat stat_1 (.icode(icode), .imemerror(imemError), .dmemerror(dmemError), .statWrite(statWrite), .statVal(statVal));
  PCIncSrc pcincsrc_1 (.icode(icode), .PCIncSrc(PCIncSrc));
  valCsrc valcsrc_1 (.icode(icode), .valCsrc(valCsrc));
  valArc valarc_1 (.icode(icode), .valAsrc(valAsrc));
  valBsrc valbsrc_1 (.icode(icode), .valBsrc(valBsrc));
  aluAsrc aluasrc_1 (.icode(icode), .aluAsrc(aluAsrc));
  aluBsrc alubsrc_1 (.icode(icode), .aluBsrc(aluBsrc));
  aluOp aluop_1 (.icode(icode), .aluOp(aluOp));
  setCC setcc_1 (.icode(icode), .setCC(setCC));
  dmemAddr dmemaddr_1 (.icode(icode), .dmemAddr(dmemAddr));
  dmemData dmemdata_1 (.icode(icode), .dmemData(dmemData));
  dmemWrite dmemwrite_1 (.icode(icode), .dmemWrite(dmemWrite));
  dstMsrc dstmsrc_1 (.icode(icode), .dstMsrc(dstMsrc));
  dstEsrc dstesrc_1 (.icode(icode), .Cnd(cond_1_cnd), .dstEsrc(dstEsrc));
  newPC newpc_1 (.icode(icode), .Cnd(cond_1_cnd), .newPC(newPC));
  Cond cond_1 (.CC(CC), .ifun(ifun), .Cnd(cond_1_cnd));
endmodule
