// Logisim project alulibrary.circ as structural Verilog: 7 circuits, main circuit Add32
module Add32 (
  input  [31:0] A32,
  input  [31:0] B32,
  input  Cin,
  output [31:0] F32,
  output Cout
);

  Adder #(.width(32)) adder_1 (.a(A32), .b(B32), .out(F32), .cin(Cin), .cout(Cout));
endmodule

module And32 (
  input  [31:0] A32,
  input  [31:0] B32,
  output [31:0] F32
);

  assign F32 = A32 & B32;  // AND_Gate and_1, 32 bits wide
endmodule

module Xor32 (
  input  [31:0] A32,
  input  [31:0] B32,
  output [31:0] F32
);

  assign F32 = A32 ^ B32;  // XOR_Gate xor_1, 32 bits wide
endmodule

module _2_1Mux32 (
  input  [31:0] A32,
  input  [31:0] B32,
  input  S,
  output [31:0] F32
);

  Multiplexer #(.width(32), .disabled(0), .enable("false")) multiplexer_1 (.in0(A32), .in1(B32), .out(F32), .sel(S));
endmodule

module _4_1Mux32 (
  input  [31:0] A32,
  input  [31:0] B32,
  input  [31:0] C32,
  input  [31:0] D32,
  input  [1:0] S2,
  output [31:0] F32
);

  Multiplexer #(.select(2), .width(32), .disabled(0), .enable("false")) multiplexer_1 (
    .in0(A32), .in1(B32), .in2(C32), .in3(D32), .out(F32), .sel(S2));
endmodule

module ShiftR32 (
  input  [31:0] A32,
  input  Cin,
  output [31:0] F32,
  output Cout
);


  assign Cout = 1'b0;
  assign F32 = {32{1'b0}};
endmodule

module ShiftL32 (
  input  [31:0] A32,
  input  Cin,
  output [31:0] F32,
  output Cout
);


  assign Cout = 1'b0;
  assign F32 = {32{1'b0}};
endmodule
