// Logisim project controllibrary.circ as structural Verilog: 17 circuits, main circuit continue
module \continue  (
  input  [1:0] Stat,
  output \continue 
);

  wire not_1_out, not_2_out;

  not not_1 (not_1_out, Stat[0]);
  not not_2 (not_2_out, Stat[1]);
  and and_1 (\continue , not_1_out, not_2_out);
endmodule

module stat (
  input  [3:0] icode,
  input  imemerror,
  input  dmemerror,
  output statWrite,
  output [1:0] statVal
);

  wire and_1_out, and_2_out, comparator_1_gt, or_1_out;

  and and_1 (and_1_out, ~icode[0], ~icode[1], ~icode[2], ~icode[3]);  // AND_Gate
  Comparator #(.width(4), .mode("unsigned")) comparator_1 (
    .a(icode), .b(4'b1011), .gt(comparator_1_gt));  // open: eq, lt
  or or_1 (or_1_out, imemerror, dmemerror);
  or or_2 (statWrite, or_1_out, comparator_1_gt, and_1_out);
  and and_2 (and_2_out, or_1_out, ~comparator_1_gt);  // AND_Gate
  or or_3 (statVal[1], and_2_out, and_1_out);
  or or_4 (statVal[0], and_1_out, comparator_1_gt);
endmodule

module PCIncSrc (
  input  [3:0] icode,
  output [1:0] PCIncSrc
);

  Multiplexer #(.select(4), .width(2)) multiplexer_1 (
    .in0(2'b00), .in1(2'b00), .in2(2'b01), .in3(2'b11), .in4(2'b11), .in5(2'b11), .in6(2'b01), .in7(2'b10),
    .in8(2'b10), .in9(2'b00), .in10(2'b01), .in11(2'b01), .out(PCIncSrc), .sel(icode));  // open: in12, in13, in14, in15, en
endmodule

module aluBsrc (
  input  [3:0] icode,
  output [1:0] aluBsrc
);

  Multiplexer #(.select(4), .width(2)) multiplexer_1 (
    .in0(2'b00), .in1(2'b00), .in2(2'b00), .in3(2'b01), .in4(2'b01), .in5(2'b01), .in6(2'b00), .in7(2'b00),
    .in8(2'b11), .in9(2'b10), .in10(2'b11), .in11(2'b01), .out(aluBsrc), .sel(icode));  // open: in12, in13, in14, in15, en
endmodule

module dmemAddr (
  input  [3:0] icode,
  output [1:0] dmemAddr
);

  Multiplexer #(.select(4), .width(2)) multiplexer_1 (
    .in0(2'b10), .in1(2'b10), .in2(2'b10), .in3(2'b10), .in4(2'b00), .in5(2'b00), .in6(2'b10), .in7(2'b10),
    .in8(2'b00), .in9(2'b01), .in10(2'b00), .in11(2'b00), .out(dmemAddr), .sel(icode));  // open: in12, in13, in14, in15, en
endmodule

module dstEsrc (
  input  [3:0] icode,
  input  Cnd,
  output [1:0] dstEsrc
);

  wire [1:1] not_1_out;

  not not_1 (not_1_out[1], Cnd);
  Multiplexer #(.select(4), .width(2)) multiplexer_1 (
    .in0(2'b10), .in1(2'b10), .in2({not_1_out[1], 1'b0}), .in3(2'b00), .in4(2'b10), .in5(2'b10), .in6(2'b00),
    .in7(2'b10), .in8(2'b01), .in9(2'b01), .in10(2'b01), .in11(2'b01), .out(dstEsrc), .sel(icode));  // open: in12, in13, in14, in15, en
endmodule

module newPC (
  input  [3:0] icode,
  input  Cnd,
  output [1:0] newPC
);

  Multiplexer #(.select(4), .width(2)) multiplexer_1 (
    .in0(2'b00), .in1(2'b00), .in2(2'b00), .in3(2'b00), .in4(2'b00), .in5(2'b00), .in6(2'b00),
    .in7({1'b0, Cnd}), .in8(2'b01), .in9(2'b10), .in10(2'b00), .in11(2'b00), .out(newPC), .sel(icode));  // open: in12, in13, in14, in15, en
endmodule

module valCsrc (
  input  [3:0] icode,
  output valCsrc
);

  Multiplexer #(.select(4)) multiplexer_1 (
    .in0(1'b0), .in1(1'b0), .in2(1'b0), .in3(1'b1), .in4(1'b1), .in5(1'b1), .in6(1'b0), .in7(1'b0),
    .in8(1'b0), .in9(1'b0), .in10(1'b0), .in11(1'b0), .out(valCsrc), .sel(icode));  // open: in12, in13, in14, in15, en

  // Notes on the sheet:
  //   valCsrc: pull=down
endmodule

module valArc (
  input  [3:0] icode,
  output valAsrc
);

  Multiplexer #(.select(4)) multiplexer_1 (
    .in0(1'b0), .in1(1'b0), .in2(1'b0), .in3(1'b0), .in4(1'b0), .in5(1'b0), .in6(1'b0), .in7(1'b0),
    .in8(1'b0), .in9(1'b1), .in10(1'b0), .in11(1'b1), .out(valAsrc), .sel(icode));  // open: in12, in13, in14, in15, en
endmodule

module valBsrc (
  input  [3:0] icode,
  output valBsrc
);

  Multiplexer #(.select(4)) multiplexer_1 (
    .in0(1'b0), .in1(1'b0), .in2(1'b0), .in3(1'b0), .in4(1'b0), .in5(1'b0), .in6(1'b0), .in7(1'b0),
    .in8(1'b1), .in9(1'b1), .in10(1'b1), .in11(1'b1), .out(valBsrc), .sel(icode));  // open: in12, in13, in14, in15, en
endmodule

module aluAsrc (
  input  [3:0] icode,
  output aluAsrc
);

  Multiplexer #(.select(4)) multiplexer_1 (
    .in0(1'b0), .in1(1'b0), .in2(1'b1), .in3(1'b1), .in4(1'b0), .in5(1'b0), .in6(1'b0), .in7(1'b0),
    .in8(1'b0), .in9(1'b0), .in10(1'b0), .in11(1'b0), .out(aluAsrc), .sel(icode));  // open: in12, in13, in14, in15, en
endmodule

module setCC (
  input  [3:0] icode,
  output setCC
);

  Multiplexer #(.select(4)) multiplexer_1 (
    .in0(1'b0), .in1(1'b0), .in2(1'b0), .in3(1'b0), .in4(1'b0), .in5(1'b0), .in6(1'b1), .in7(1'b0),
    .in8(1'b0), .in9(1'b0), .in10(1'b0), .in11(1'b0), .out(setCC), .sel(icode));  // open: in12, in13, in14, in15, en
endmodule

module aluOp (
  input  [3:0] icode,
  output aluOp
);

  Multiplexer #(.select(4)) multiplexer_1 (
    .in0(1'b0), .in1(1'b0), .in2(1'b0), .in3(1'b0), .in4(1'b0), .in5(1'b0), .in6(1'b1), .in7(1'b0),
    .in8(1'b0), .in9(1'b0), .in10(1'b0), .in11(1'b0), .out(aluOp), .sel(icode));  // open: in12, in13, in14, in15, en
endmodule

module dmemData (
  input  [3:0] icode,
  output dmemData
);

  Multiplexer #(.select(4)) multiplexer_1 (
    .in0(1'b0), .in1(1'b0), .in2(1'b0), .in3(1'b0), .in4(1'b0), .in5(1'b0), .in6(1'b0), .in7(1'b0),
    .in8(1'b1), .in9(1'b0), .in10(1'b0), .in11(1'b0), .in12(1'b0), .out(dmemData), .sel(icode));  // open: in13, in14, in15, en
endmodule

module dmemWrite (
  input  [3:0] icode,
  output dmemWrite
);

  Multiplexer #(.select(4)) multiplexer_1 (
    .in0(1'b0), .in1(1'b0), .in2(1'b0), .in3(1'b0), .in4(1'b1), .in5(1'b0), .in6(1'b0), .in7(1'b0),
    .in8(1'b1), .in9(1'b0), .in10(1'b1), .in11(1'b0), .out(dmemWrite), .sel(icode));  // open: in12, in13, in14, in15, en
endmodule

module dstMsrc (
  input  [3:0] icode,
  output dstMsrc
);

  Multiplexer #(.select(4)) multiplexer_1 (
    .in0(1'b1), .in1(1'b1), .in2(1'b1), .in3(1'b1), .in4(1'b1), .in5(1'b0), .in6(1'b1), .in7(1'b1),
    .in8(1'b1), .in9(1'b1), .in10(1'b1), .in11(1'b0), .out(dstMsrc), .sel(icode));  // open: in12, in13, in14, in15, en
endmodule

module Cond (
  input  [2:0] CC,
  input  [3:0] ifun,
  output Cnd
);

  wire and_1_out, not_1_out, not_2_out, not_3_out, not_4_out, or_1_out, xor_1_out, xor_2_out, xor_3_out,
       xor_4_out;

  not not_1 (not_1_out, CC[2]);
  xor xor_1 (xor_1_out, CC[2], CC[2]);
  xor xor_2 (xor_2_out, CC[2], CC[2]);
  xor xor_3 (xor_3_out, CC[2], CC[2]);
  xor xor_4 (xor_4_out, CC[2], CC[2]);
  or or_1 (or_1_out, CC[2], xor_1_out);
  not not_2 (not_2_out, CC[2]);
  not not_3 (not_3_out, xor_4_out);
  not not_4 (not_4_out, xor_3_out);
  and and_1 (and_1_out, not_3_out, not_1_out);
  Multiplexer #(.select(4)) multiplexer_1 (
    .in0(1'b1), .in1(or_1_out), .in2(xor_2_out), .in3(CC[2]), .in4(not_2_out), .in5(not_4_out),
    .in6(and_1_out), .out(Cnd), .sel(ifun));  // open: in7, in8, in9, in10, in11, in12, in13, in14, in15, en

  assign CC[1:0] = {2{CC[2]}};
endmodule
