// Logisim project ALU.circ as structural Verilog: 2 circuits, main circuit main
module main (
  input  [31:0] aluA,
  input  [31:0] aluB,
  input  [3:0] aluOp,
  input  Cin,
  output CF,
  output ZF,
  output SF,
  output OF,
  output [31:0] valE
);

  ALU32 alu32_1 (.aluA(aluA), .aluB(aluB), .Cin(Cin), .valE(valE), .CF(CF), .ZF(ZF), .SF(SF), .OF(OF), .aluOp(aluOp));
endmodule

module ALU32 (
  input  [31:0] aluA,
  input  [31:0] aluB,
  input  Cin,
  input  [3:0] aluOp,
  output CF,
  output ZF,
  output SF,
  output OF,
  output [31:0] valE
);

  wire add32_1_cout, notadd32_1_cout, of_add_1_out_4, of_notadd_1_out_4, shiftl32_1_cout, shiftr32_1_cout;
  wire [31:0] add32_1_f32, and32_1_f32, shiftl32_1_f32, shiftr32_1_f32, undriven, undriven_2, undriven_3,
       xor32_1_f32;

  ShiftL32 shiftl32_1 (.A32(aluA), .Cin(Cin), .F32(shiftl32_1_f32), .Cout(shiftl32_1_cout));
  ShiftR32 shiftr32_1 (.A32(aluA), .Cin(Cin), .F32(shiftr32_1_f32), .Cout(shiftr32_1_cout));
  Xor32 xor32_1 (.A32(aluA), .B32(aluB), .F32(xor32_1_f32));
  And32 and32_1 (.A32(aluA), .B32(aluB), .F32(and32_1_f32));
  NotAdd32 notadd32_1 (.A32(aluA), .B32(aluB), .Cin(Cin), .F32(undriven_3), .Cout(notadd32_1_cout));
  Add32 add32_1 (.A32(aluA), .B32(aluB), .Cin(Cin), .F32(add32_1_f32), .Cout(add32_1_cout));
  OF_Add of_add_1 (.Input1(aluA), .Input2(aluB), .Output(undriven_2), .out_4(of_add_1_out_4));
  OF_NotAdd of_notadd_1 (.Input1(aluA), .Input2(aluB), .Output(undriven), .out_4(of_notadd_1_out_4));
  _32_1_Mux1 u_32_1_mux1_1 (
    .Input1(shiftl32_1_cout), .Input5(shiftr32_1_cout), .Input9(notadd32_1_cout), .Input13(add32_1_cout),
    .Input2(1'b0), .Input6(1'b0), .Input10(1'b0), .Input14(1'b0), .Input3(1'b0), .Input7(1'b0),
    .Input11(1'b0), .Input15(1'b0), .Input4(1'b0), .Input8(1'b0), .Input12(1'b0), .Input16(1'b0), .S(CF),
    .Input17(1'b0), .Input21(1'b0), .Input25(1'b0), .Input29(1'b0), .Input18(1'b0), .Input22(1'b0),
    .Input26(1'b0), .Input30(1'b0), .Input19(1'b0), .Input23(1'b0), .Input27(1'b0), .Input31(1'b0),
    .Input20(1'b0), .Input24(1'b0), .Input28(1'b0), .Input32(1'b0), .S_2(aluOp[2]), .S_3(aluOp[3]),
    .S_0(aluOp[0]), .S_1(aluOp[1]));  // open: S_4
  _32_1_Mux1 u_32_1_mux1_2 (
    .Input1(1'b0), .Input5(1'b0), .Input9(1'b0), .Input13(1'b0), .Input2(1'b0), .Input6(1'b0),
    .Input10(1'b0), .Input14(1'b0), .Input3(1'b0), .Input7(1'b0), .Input11(1'b0), .Input15(1'b0),
    .Input4(1'b0), .Input8(1'b0), .Input12(of_add_1_out_4), .Input16(of_notadd_1_out_4), .S(OF),
    .Input17(1'b0), .Input21(1'b0), .Input25(1'b0), .Input29(1'b0), .Input18(1'b0), .Input22(1'b0),
    .Input26(1'b0), .Input30(1'b0), .Input19(1'b0), .Input23(1'b0), .Input27(1'b0), .Input31(1'b0),
    .Input20(1'b0), .Input24(1'b0), .Input28(1'b0), .Input32(1'b0), .S_2(aluOp[2]), .S_3(aluOp[3]),
    .S_0(aluOp[0]), .S_1(aluOp[1]));  // open: S_4
  _32_1_Mux32 u_32_1_mux32_1 (
    .Input1({32{1'b0}}), .Input9({32{1'b0}}), .Input2({32{1'b0}}), .Input10({32{1'b0}}), .Input3({32{1'b0}}),
    .Input11({32{1'b0}}), .Input4({32{1'b0}}), .Input12({32{1'b0}}), .Input5(shiftl32_1_f32),
    .Input13(shiftr32_1_f32), .Input6(xor32_1_f32), .Input14(and32_1_f32), .Input7(undriven_3),
    .Input15(add32_1_f32), .Input8(undriven), .Input16(undriven_2), .S_0(aluOp), .Output(valE),
    .Input17({32{1'b0}}), .Input25({32{1'b0}}), .Input18({32{1'b0}}), .Input26({32{1'b0}}),
    .Input19({32{1'b0}}), .Input27({32{1'b0}}), .Input20({32{1'b0}}), .Input28({32{1'b0}}),
    .Input21({32{1'b0}}), .Input29({32{1'b0}}), .Input22({32{1'b0}}), .Input30({32{1'b0}}),
    .Input23({32{1'b0}}), .Input31({32{1'b0}}), .Input24({32{1'b0}}), .Input32({32{1'b0}}));  // open: S_1
  ZF zf_1 (.ZF(ZF), .Input(valE));
  SF sf_1 (.OF(SF), .Input(valE));
endmodule
