// Logisim project ALU.circ as structural Verilog: 2 circuits, main circuit main
module main (
  input  [31:0] aluA,
  input  [31:0] aluB,
  input  [3:0] aluOp,
  input  Cin,
  output CF,
  output ZF,
  output SF,
  output OF,
  output [31:0] valE
);

  ALU32 alu32_1 (.aluA(aluA), .aluB(aluB), .Cin(Cin), .valE(valE), .CF(CF), .ZF(ZF), .SF(SF), .OF(OF), .aluOp(aluOp));
endmodule

module ALU32 (
  input  [31:0] aluA,
  input  [31:0] aluB,
  input  Cin,
  input  [3:0] aluOp,
  output ZF,
  output SF,
  output OF,
  output CF,
  output [31:0] valE
);

  wire add32_1_cout, add32_3_cout, multiplexer_1_out, multiplexer_3_out, shiftl32_1_cout, shiftr32_1_cout;
  wire [31:0] add32_1_f32, add32_2_f32, add32_3_f32, add32_4_f32, add32_5_f32, add32_6_f32, and32_1_f32,
       and32_2_f32, n2_1mux32_1_f32, n2_1mux32_2_f32, n2_1mux32_3_f32, not_1_out, not_2_out, not_3_out,
       not_4_out, not_5_out, not_6_out, not_7_out, not_8_out, or_1_out, or_2_out, or_3_out, shiftl32_1_f32,
       shiftr32_1_f32, xor32_1_f32, xor32_2_f32, xor32_3_f32;

  assign not_1_out = ~aluB;  // NOT_Gate not_1, 32 bits wide
  Multiplexer #(.disabled(0), .enable("false")) multiplexer_1 (
    .in0(add32_1_cout), .in1(add32_3_cout), .out(multiplexer_1_out), .sel(aluOp[0]));
  Add32 add32_1 (.A32(aluA), .B32(aluB), .Cin(Cin), .F32(add32_1_f32), .Cout(add32_1_cout));
  Add32 add32_2 (.A32(not_1_out), .B32(32'h1), .Cin(Cin), .F32(add32_2_f32));  // open: Cout
  And32 and32_1 (.A32(aluA), .B32(aluB), .F32(and32_1_f32));
  Xor32 xor32_1 (.A32(aluA), .B32(aluB), .F32(xor32_1_f32));
  ShiftR32 shiftr32_1 (.A32(aluA), .Cin(Cin), .F32(shiftr32_1_f32), .Cout(shiftr32_1_cout));
  ShiftL32 shiftl32_1 (.A32(aluA), .Cin(Cin), .F32(shiftl32_1_f32), .Cout(shiftl32_1_cout));
  Multiplexer #(.select(2), .disabled(0), .enable("false")) multiplexer_2 (
    .in0(multiplexer_1_out), .in1(1'b0), .in2(multiplexer_3_out), .in3(1'b0), .out(CF), .sel(aluOp[2:1]));
  Multiplexer #(.disabled(0), .enable("false")) multiplexer_3 (
    .in0(shiftr32_1_cout), .in1(shiftl32_1_cout), .out(multiplexer_3_out), .sel(aluOp[0]));
  Add32 add32_3 (.A32(aluA), .B32(add32_2_f32), .Cin(Cin), .F32(add32_3_f32), .Cout(add32_3_cout));
  _2_1Mux32 u_2_1mux32_1 (.A32(and32_1_f32), .B32(xor32_1_f32), .F32(n2_1mux32_1_f32), .S(aluOp[0]));
  _2_1Mux32 u_2_1mux32_2 (.A32(shiftr32_1_f32), .B32(shiftl32_1_f32), .F32(n2_1mux32_2_f32), .S(aluOp[0]));
  assign not_2_out = ~or_1_out;  // NOT_Gate not_2, 32 bits wide
  assign or_1_out = add32_4_f32 | n2_1mux32_3_f32;  // OR_Gate or_1, 32 bits wide
  Add32 add32_4 (.A32(not_3_out), .B32(32'h1), .F32(add32_4_f32));  // open: Cin, Cout
  assign not_3_out = ~n2_1mux32_3_f32;  // NOT_Gate not_3, 32 bits wide
  Multiplexer #(.select(2), .disabled(0), .enable("false")) multiplexer_4 (
    .in0(not_2_out[31]), .in1(not_5_out[31]), .in2(not_7_out[31]), .out(ZF), .sel(aluOp[2:1]));  // open: in3
  Add32 add32_5 (.A32(not_4_out), .B32(32'h1), .F32(add32_5_f32));  // open: Cin, Cout
  assign not_4_out = ~n2_1mux32_1_f32;  // NOT_Gate not_4, 32 bits wide
  _2_1Mux32 u_2_1mux32_3 (.A32(add32_1_f32), .B32(add32_3_f32), .F32(n2_1mux32_3_f32), .S(aluOp[0]));
  assign not_5_out = ~or_2_out;  // NOT_Gate not_5, 32 bits wide
  assign or_2_out = add32_5_f32 | n2_1mux32_1_f32;  // OR_Gate or_2, 32 bits wide
  Add32 add32_6 (.A32(not_6_out), .B32(32'h1), .F32(add32_6_f32));  // open: Cin, Cout
  assign not_6_out = ~n2_1mux32_2_f32;  // NOT_Gate not_6, 32 bits wide
  assign not_7_out = ~or_3_out;  // NOT_Gate not_7, 32 bits wide
  assign or_3_out = add32_6_f32 | n2_1mux32_2_f32;  // OR_Gate or_3, 32 bits wide
  _4_1Mux32 u_4_1mux32_1 (
    .A32(n2_1mux32_3_f32), .B32(n2_1mux32_1_f32), .C32(n2_1mux32_2_f32), .F32(valE), .S2(aluOp[2:1]));  // open: D32
  Multiplexer #(.select(2), .disabled(0), .enable("false")) multiplexer_5 (
    .in0(n2_1mux32_3_f32[31]), .in1(n2_1mux32_1_f32[31]), .in2(n2_1mux32_2_f32[31]), .in3(1'b0), .out(SF),
    .sel(aluOp[2:1]));
  And32 and32_2 (.A32(xor32_2_f32), .B32(not_8_out), .F32(and32_2_f32));
  Xor32 xor32_2 (.A32(n2_1mux32_3_f32), .B32(aluA), .F32(xor32_2_f32));
  Multiplexer #(.select(2), .disabled(0), .enable("false")) multiplexer_6 (
    .in0(and32_2_f32[31]), .in1(1'b0), .in2(1'b0), .in3(1'b0), .out(OF), .sel(aluOp[2:1]));
  assign not_8_out = ~xor32_3_f32;  // NOT_Gate not_8, 32 bits wide
  Xor32 xor32_3 (.A32(aluA), .B32(aluB), .F32(xor32_3_f32));

  // Notes on the sheet:
  //   aluA
  //   Cin
  //   aluB
endmodule
