// Logisim project Y86Control.circ as structural Verilog: 1 circuit, main circuit Y86Control
module Y86Control (
  input  [3:0] icode,
  input  [3:0] ifun,
  input  [2:0] CC,
  input  [1:0] Stat,
  input  imemError,
  input  dmemError,
  output \continue ,
  output statWrite,
  output [1:0] statVal,
  output [1:0] PCIncSrc,
  output valCsrc,
  output valAsrc,
  output valBsrc,
  output [1:0] aluAsrc,
  output aluBsrc,
  output setCC,
  output aluOp,
  output [1:0] dmemAddr,
  output dmemData,
  output dmemWrite,
  output [1:0] dstEsrc,
  output dstMsrc,
  output [1:0] newPC
);


  assign aluAsrc = 2'b00;
  assign aluBsrc = 1'b0;
  assign aluOp = 1'b0;
  assign \continue  = 1'b0;
  assign dmemAddr = 2'b00;
  assign dmemData = 1'b0;
  assign dmemWrite = 1'b0;
  assign dstEsrc = 2'b00;
  assign dstMsrc = 1'b0;
  assign newPC = 2'b00;
  assign PCIncSrc = 2'b00;
  assign setCC = 1'b0;
  assign statVal = 2'b00;
  assign statWrite = 1'b0;
  assign valAsrc = 1'b0;
  assign valBsrc = 1'b0;
  assign valCsrc = 1'b0;
endmodule
