// Logisim project Y86Memory.circ as structural Verilog: 4 circuits, main circuit Memory
module Memory (
  input  [31:0] ReadAddr,
  output [7:0] B0,
  output [7:0] B1,
  output [7:0] B2,
  output [7:0] B3,
  output [7:0] B4,
  output [7:0] B5,
  output imemError
);

  wire bankaddr_1_error, bankaddr_2_error, bankaddr_3_error, bankaddr_4_error;
  wire [2:0] low3_1_out_2;
  wire [9:0] bankaddr_1_addrout, bankaddr_2_addrout, bankaddr_3_addrout, bankaddr_4_addrout;
  wire [15:0] rom_1_data, rom_2_data, rom_3_data, rom_4_data;

  Low3 low3_1 (.in_1(ReadAddr), .out_2(low3_1_out_2));
  BankAddr bankaddr_1 (.Index(2'b00), .Address(ReadAddr), .AddrOut(bankaddr_1_addrout), .Error(bankaddr_1_error));
  BankAddr bankaddr_2 (.Index(2'b01), .Address(ReadAddr), .AddrOut(bankaddr_2_addrout), .Error(bankaddr_2_error));
  BankAddr bankaddr_3 (.Index(2'b10), .Address(ReadAddr), .AddrOut(bankaddr_3_addrout), .Error(bankaddr_3_error));
  BankAddr bankaddr_4 (.Index(2'b11), .Address(ReadAddr), .AddrOut(bankaddr_4_addrout), .Error(bankaddr_4_error));
  or or_1 (imemError, bankaddr_4_error, bankaddr_3_error, bankaddr_2_error, bankaddr_1_error);
  ROM #(.addrWidth(10), .dataWidth(16)) rom_1 (.addr(bankaddr_1_addrout), .data(rom_1_data));  // open: sel
  ROM #(.addrWidth(10), .dataWidth(16)) rom_2 (.addr(bankaddr_2_addrout), .data(rom_2_data));  // open: sel
  ROM #(.addrWidth(10), .dataWidth(16)) rom_3 (.addr(bankaddr_3_addrout), .data(rom_3_data));  // open: sel
  ROM #(.addrWidth(10), .dataWidth(16)) rom_4 (.addr(bankaddr_4_addrout), .data(rom_4_data));  // open: sel
  BankMux bankmux_1 (
    .S0(rom_1_data[15:8]), .S1(rom_1_data[7:0]), .S2(rom_2_data[15:8]), .S3(rom_2_data[7:0]),
    .S4(rom_3_data[15:8]), .S6(rom_3_data[7:0]), .S6_2(rom_4_data[15:8]), .S7(rom_4_data[7:0]),
    .AddrLow(low3_1_out_2), .Index(3'b000), .out_11(B0));
  BankMux bankmux_2 (
    .S0(rom_1_data[15:8]), .S1(rom_1_data[7:0]), .S2(rom_2_data[15:8]), .S3(rom_2_data[7:0]),
    .S4(rom_3_data[15:8]), .S6(rom_3_data[7:0]), .S6_2(rom_4_data[15:8]), .S7(rom_4_data[7:0]),
    .AddrLow(low3_1_out_2), .Index(3'b001), .out_11(B1));
  BankMux bankmux_3 (
    .S0(rom_1_data[15:8]), .S1(rom_1_data[7:0]), .S2(rom_2_data[15:8]), .S3(rom_2_data[7:0]),
    .S4(rom_3_data[15:8]), .S6(rom_3_data[7:0]), .S6_2(rom_4_data[15:8]), .S7(rom_4_data[7:0]),
    .AddrLow(low3_1_out_2), .Index(3'b010), .out_11(B2));
  BankMux bankmux_4 (
    .S0(rom_1_data[15:8]), .S1(rom_1_data[7:0]), .S2(rom_2_data[15:8]), .S3(rom_2_data[7:0]),
    .S4(rom_3_data[15:8]), .S6(rom_3_data[7:0]), .S6_2(rom_4_data[15:8]), .S7(rom_4_data[7:0]),
    .AddrLow(low3_1_out_2), .Index(3'b011), .out_11(B3));
  BankMux bankmux_5 (
    .S0(rom_1_data[15:8]), .S1(rom_1_data[7:0]), .S2(rom_2_data[15:8]), .S3(rom_2_data[7:0]),
    .S4(rom_3_data[15:8]), .S6(rom_3_data[7:0]), .S6_2(rom_4_data[15:8]), .S7(rom_4_data[7:0]),
    .AddrLow(low3_1_out_2), .Index(3'b100), .out_11(B4));
  BankMux bankmux_6 (
    .S0(rom_1_data[15:8]), .S1(rom_1_data[7:0]), .S2(rom_2_data[15:8]), .S3(rom_2_data[7:0]),
    .S4(rom_3_data[15:8]), .S6(rom_3_data[7:0]), .S6_2(rom_4_data[15:8]), .S7(rom_4_data[7:0]),
    .AddrLow(low3_1_out_2), .Index(3'b101), .out_11(B5));

  // Notes on the sheet:
  //   contents of rom_1 (hex, n*v repeats v):
  //   30f0 300 6031 4006 400
  //   contents of rom_2 (hex, n*v repeats v):
  //   500 0 30f6
  //   contents of rom_3 (hex, n*v repeats v):
  //   0 6030 2800
  //   contents of rom_4 (hex, n*v repeats v):
  //   30f3 6001 0 4016
endmodule

module BankMux (
  input  [7:0] S0,
  input  [7:0] S1,
  input  [7:0] S2,
  input  [7:0] S3,
  input  [7:0] S4,
  input  [7:0] S6,
  input  [7:0] S6_2,
  input  [7:0] S7,
  input  [2:0] AddrLow,
  input  [2:0] Index,
  output [7:0] out_11
);

  wire [2:0] adder_1_out;

  Multiplexer #(.select(3), .width(8), .enable("false")) multiplexer_1 (
    .in0(S0), .in1(S1), .in2(S2), .in3(S3), .in4(S4), .in5(S6), .in6(S6_2), .in7(S7), .out(out_11),
    .sel(adder_1_out));
  Adder #(.width(3)) adder_1 (.a(AddrLow), .b(Index), .out(adder_1_out), .cin(1'b0));  // open: cout
endmodule

module BankAddr (
  input  [1:0] Index,
  input  [31:0] Address,
  output [9:0] AddrOut,
  output Error
);

  wire subtractor_1_bout;

  // Probe on Address
  // Probe on Address[2:1]
  Subtractor #(.width(2)) subtractor_1 (.a(Index), .b(Address[2:1]), .bout(subtractor_1_bout));  // open: out, bin
  Adder #(.width(10)) adder_1 (
    .a({10{1'b0}}), .b(Address[12:3]), .out(AddrOut), .cin(subtractor_1_bout));  // open: cout
  or or_1 (Error, Address[13], Address[14], Address[15], Address[16], Address[17], Address[18], Address[19], Address[20], Address[21], Address[22], Address[23], Address[24], Address[25], Address[26], Address[27], Address[28], Address[29], Address[30], Address[31]);
endmodule

module Low3 (
  input  [31:0] in_1,
  output [2:0] out_2
);


  assign out_2 = in_1[2:0];
endmodule
