// Logisim project alulibrary.circ as structural Verilog: 16 circuits, main circuit Add32
module Add32 (
  input  [31:0] A32,
  input  [31:0] B32,
  input  Cin,
  output [31:0] F32,
  output Cout
);

  Adder #(.width(32)) adder_1 (.a(A32), .b(B32), .out(F32), .cin(Cin), .cout(Cout));
endmodule

module And32 (
  input  [31:0] A32,
  input  [31:0] B32,
  output [31:0] F32
);

  assign F32 = A32 & B32;  // AND_Gate and_1, 32 bits wide
endmodule

module Xor32 (
  input  [31:0] A32,
  input  [31:0] B32,
  output [31:0] F32
);

  assign F32 = A32 ^ B32;  // XOR_Gate xor_1, 32 bits wide
endmodule

module _2_1Mux32 (
  input  [31:0] A32,
  input  [31:0] B32,
  input  S,
  output [31:0] F32
);

  Multiplexer #(.width(32), .disabled(0), .enable("false")) multiplexer_1 (.in0(A32), .in1(B32), .out(F32), .sel(S));
endmodule

module _4_1Mux32 (
  input  [31:0] A32,
  input  [31:0] B32,
  input  [31:0] C32,
  input  [31:0] D32,
  input  [1:0] S2,
  output [31:0] F32
);

  Multiplexer #(.select(2), .width(32), .disabled(0), .enable("false")) multiplexer_1 (
    .in0(A32), .in1(B32), .in2(C32), .in3(D32), .out(F32), .sel(S2));
endmodule

module ShiftR32 (
  input  [31:0] A32,
  input  Cin,
  output [31:0] F32,
  output Cout
);


  assign Cout = A32[0];
  assign F32 = {Cin, A32[31:1]};
endmodule

module ShiftL32 (
  input  [31:0] A32,
  input  Cin,
  output [31:0] F32,
  output Cout
);


  assign Cout = A32[31];
  assign F32 = {A32[30:0], Cin};
endmodule

module ZF (
  input  [31:0] Input,
  output ZF
);

  wire and_1_out, and_2_out, and_3_out, and_4_out, and_5_out, and_6_out, and_7_out, and_8_out, and_9_out,
       and_10_out, and_11_out, and_12_out, and_13_out, and_14_out, and_15_out, and_17_out, and_18_out,
       and_19_out, and_20_out, and_21_out, and_22_out, and_23_out, and_24_out, and_25_out, and_26_out,
       and_27_out, and_28_out, and_29_out, and_30_out, and_31_out, not_1_out, not_2_out, not_3_out,
       not_4_out, not_5_out, not_6_out, not_7_out, not_8_out, not_9_out, not_10_out, not_11_out, not_12_out,
       not_13_out, not_14_out, not_15_out, not_16_out, not_17_out, not_18_out, not_19_out, not_20_out,
       not_21_out, not_22_out, not_23_out, not_24_out, not_25_out, not_26_out, not_27_out, not_28_out,
       not_29_out, not_30_out, not_31_out, not_32_out;

  and and_1 (and_1_out, and_3_out, and_2_out);
  and and_2 (and_2_out, not_2_out, not_1_out);
  and and_3 (and_3_out, not_5_out, not_3_out);
  and and_4 (and_4_out, and_1_out, and_5_out);
  and and_5 (and_5_out, and_6_out, and_9_out);
  and and_6 (and_6_out, not_4_out, not_9_out);
  and and_7 (and_7_out, and_4_out, and_10_out);
  and and_8 (and_8_out, not_7_out, not_12_out);
  and and_9 (and_9_out, not_8_out, not_6_out);
  and and_10 (and_10_out, and_11_out, and_14_out);
  and and_11 (and_11_out, and_8_out, and_13_out);
  and and_12 (and_12_out, not_13_out, not_21_out);
  and and_13 (and_13_out, not_11_out, not_10_out);
  not not_1 (not_1_out, Input[28]);
  not not_2 (not_2_out, Input[29]);
  not not_3 (not_3_out, Input[30]);
  not not_4 (not_4_out, Input[27]);
  not not_5 (not_5_out, Input[31]);
  and and_14 (and_14_out, and_12_out, and_15_out);
  and and_15 (and_15_out, not_15_out, not_19_out);
  not not_6 (not_6_out, Input[24]);
  not not_7 (not_7_out, Input[23]);
  not not_8 (not_8_out, Input[25]);
  not not_9 (not_9_out, Input[26]);
  not not_10 (not_10_out, Input[20]);
  not not_11 (not_11_out, Input[21]);
  not not_12 (not_12_out, Input[22]);
  not not_13 (not_13_out, Input[19]);
  and and_16 (ZF, and_7_out, and_25_out);
  and and_17 (and_17_out, and_18_out, and_21_out);
  and and_18 (and_18_out, not_18_out, not_14_out);
  not not_14 (not_14_out, Input[14]);
  not not_15 (not_15_out, Input[17]);
  not not_16 (not_16_out, Input[13]);
  not not_17 (not_17_out, Input[12]);
  not not_18 (not_18_out, Input[15]);
  not not_19 (not_19_out, Input[16]);
  not not_20 (not_20_out, Input[11]);
  not not_21 (not_21_out, Input[18]);
  and and_19 (and_19_out, and_17_out, and_22_out);
  and and_20 (and_20_out, not_20_out, not_25_out);
  and and_21 (and_21_out, not_16_out, not_17_out);
  not not_22 (not_22_out, Input[4]);
  not not_23 (not_23_out, Input[6]);
  not not_24 (not_24_out, Input[9]);
  not not_25 (not_25_out, Input[10]);
  not not_26 (not_26_out, Input[8]);
  not not_27 (not_27_out, Input[7]);
  not not_28 (not_28_out, Input[5]);
  not not_29 (not_29_out, Input[3]);
  and and_22 (and_22_out, and_20_out, and_23_out);
  and and_23 (and_23_out, not_24_out, not_26_out);
  and and_24 (and_24_out, not_27_out, not_23_out);
  not not_30 (not_30_out, Input[2]);
  not not_31 (not_31_out, Input[0]);
  not not_32 (not_32_out, Input[1]);
  and and_25 (and_25_out, and_19_out, and_28_out);
  and and_26 (and_26_out, and_24_out, and_27_out);
  and and_27 (and_27_out, not_28_out, not_22_out);
  and and_28 (and_28_out, and_26_out, and_29_out);
  and and_29 (and_29_out, and_31_out, and_30_out);
  and and_30 (and_30_out, not_32_out, not_31_out);
  and and_31 (and_31_out, not_29_out, not_30_out);
endmodule

module SF (
  input  [31:0] Input,
  output OF
);


  assign OF = Input[31];
endmodule

module OF_Add (
  input  [31:0] Input1,
  input  [31:0] Input2,
  input  [31:0] Output,
  output out_4
);

  wire and_1_out, and_2_out, and_3_out, and_4_out, not_1_out, not_2_out, not_3_out, not_4_out, or_1_out,
       xor_1_out;

  and and_1 (and_1_out, Input2[31], Input1[31]);
  and and_2 (and_2_out, Output[31], and_1_out);
  not not_1 (not_1_out, and_2_out);
  not not_2 (not_2_out, Input1[31]);
  not not_3 (not_3_out, Input2[31]);
  not not_4 (not_4_out, Output[31]);
  and and_3 (and_3_out, not_4_out, and_4_out);
  and and_4 (and_4_out, not_3_out, not_2_out);
  xor xor_1 (xor_1_out, and_3_out, not_1_out);
  or or_1 (or_1_out, and_4_out, and_1_out);
  and and_5 (out_4, or_1_out, xor_1_out);
endmodule

module OF_NotAdd (
  input  [31:0] Input1,
  input  [31:0] Input2,
  input  [31:0] Output,
  output out_4
);

  wire and_1_out, and_2_out, and_3_out, and_4_out, not_1_out, not_2_out, not_3_out, not_4_out, not_5_out,
       xor_1_out, xor_2_out;

  not not_1 (not_1_out, Output[31]);
  and and_1 (and_1_out, not_1_out, Input2[31]);
  xor xor_1 (xor_1_out, Input2[31], Input1[31]);
  and and_2 (and_2_out, and_1_out, xor_1_out);
  or or_1 (out_4, and_2_out, and_4_out);
  not not_2 (not_2_out, Input1[31]);
  not not_3 (not_3_out, Input2[31]);
  not not_4 (not_4_out, Output[31]);
  not not_5 (not_5_out, not_4_out);
  and and_3 (and_3_out, not_5_out, not_3_out);
  xor xor_2 (xor_2_out, not_3_out, not_2_out);
  and and_4 (and_4_out, and_3_out, xor_2_out);
endmodule

module NotAdd32 (
  input  [31:0] A32,
  input  [31:0] F32,
  input  [31:0] B32,
  input  Cin,
  output Cout
);

  wire [31:0] not_1_out;

  assign not_1_out = ~A32;  // NOT_Gate not_1, 32 bits wide
  Adder #(.width(32)) adder_1 (.a(not_1_out), .b(B32), .out(F32), .cin(Cin), .cout(Cout));
endmodule

module _32_1_Mux32 (
  input  [31:0] Input1,
  input  [31:0] Input9,
  input  [31:0] Input17,
  input  [31:0] Input25,
  input  [31:0] Input2,
  input  [31:0] Input10,
  input  [31:0] Input18,
  input  [31:0] Input26,
  input  [31:0] Input3,
  input  [31:0] Input11,
  input  [31:0] Input19,
  input  [31:0] Input27,
  input  [31:0] Input4,
  input  [31:0] Input12,
  input  [31:0] Input20,
  input  [31:0] Input28,
  input  [31:0] Input5,
  input  [31:0] Input13,
  input  [31:0] Input21,
  input  [31:0] Input29,
  input  [31:0] Input6,
  input  [31:0] Input14,
  input  [31:0] Input22,
  input  [31:0] Input30,
  input  [31:0] Input7,
  input  [31:0] Input15,
  input  [31:0] Input23,
  input  [31:0] Input31,
  input  [31:0] Input8,
  input  [31:0] Input16,
  input  [31:0] Input24,
  input  [31:0] Input32,
  input  S_1,
  input  [31:0] Output,
  input  [3:0] S_0
);

  wire [31:0] multiplexer_1_out, multiplexer_3_out;

  Multiplexer #(.select(4), .width(32), .disabled(0), .enable("false")) multiplexer_1 (
    .in0(Input8), .in1(Input7), .in2(Input6), .in3(Input5), .in4(Input4), .in5(Input3), .in6(Input2),
    .in7(Input1), .in8(Input16), .in9(Input15), .in10(Input14), .in11(Input13), .in12(Input12),
    .in13(Input11), .in14(Input10), .in15(Input9), .out(multiplexer_1_out), .sel(S_0));
  Multiplexer #(.width(32), .disabled(0), .enable("false")) multiplexer_2 (
    .in0(multiplexer_1_out), .in1(multiplexer_3_out), .out(Output), .sel(S_1));
  Multiplexer #(.select(4), .width(32), .disabled(0), .enable("false")) multiplexer_3 (
    .in0(Input17), .in1(Input18), .in2(Input19), .in3(Input20), .in4(Input21), .in5(Input22), .in6(Input23),
    .in7(Input24), .in8(Input25), .in9(Input26), .in10(Input27), .in11(Input28), .in12(Input29),
    .in13(Input30), .in14(Input31), .in15(Input32), .out(multiplexer_3_out), .sel(S_0));
endmodule

module _2_1_Mux1 (
  input  S_0,
  input  A,
  input  B,
  output S
);

  wire and_1_out, and_2_out, not_1_out;

  and and_1 (and_1_out, S_0, A);
  not not_1 (not_1_out, S_0);
  and and_2 (and_2_out, not_1_out, B);
  or or_1 (S, and_1_out, and_2_out);
endmodule

module _4_1_Mux1 (
  input  S_0,
  input  S_1,
  input  A,
  input  B,
  input  C,
  input  D,
  output S
);

  wire n2_1_mux1_1_s, n2_1_mux1_2_s;

  _2_1_Mux1 u_2_1_mux1_1 (.S_0(S_0), .A(A), .B(B), .S(n2_1_mux1_1_s));
  _2_1_Mux1 u_2_1_mux1_2 (.S_0(S_0), .A(C), .B(D), .S(n2_1_mux1_2_s));
  _2_1_Mux1 u_2_1_mux1_3 (.S_0(S_1), .A(n2_1_mux1_1_s), .B(n2_1_mux1_2_s), .S(S));
endmodule

module _32_1_Mux1 (
  input  Input1,
  input  Input5,
  input  Input9,
  input  Input13,
  input  Input17,
  input  Input21,
  input  Input25,
  input  Input29,
  input  Input2,
  input  Input6,
  input  Input10,
  input  Input14,
  input  Input18,
  input  Input22,
  input  Input26,
  input  Input30,
  input  Input3,
  input  Input7,
  input  Input11,
  input  Input15,
  input  Input19,
  input  Input23,
  input  Input27,
  input  Input31,
  input  Input4,
  input  Input8,
  input  Input12,
  input  Input16,
  input  Input20,
  input  Input24,
  input  Input28,
  input  Input32,
  input  S_4,
  input  S_2,
  input  S_3,
  input  S_0,
  input  S_1,
  output S
);

  wire n2_1_mux1_1_s, n2_1_mux1_2_s, n2_1_mux1_3_s, n2_1_mux1_4_s, n2_1_mux1_5_s, n2_1_mux1_6_s,
       n2_1_mux1_7_s, n4_1_mux1_1_s, n4_1_mux1_2_s, n4_1_mux1_3_s, n4_1_mux1_4_s, n4_1_mux1_5_s,
       n4_1_mux1_6_s, n4_1_mux1_7_s, n4_1_mux1_8_s;

  _4_1_Mux1 u_4_1_mux1_1 (.S_0(Input1), .S_1(Input2), .A(Input3), .B(Input4), .C(S_0), .D(S_1), .S(n4_1_mux1_1_s));
  _4_1_Mux1 u_4_1_mux1_2 (.S_0(Input5), .S_1(Input6), .A(Input7), .B(Input8), .C(S_0), .D(S_1), .S(n4_1_mux1_2_s));
  _2_1_Mux1 u_2_1_mux1_1 (.S_0(n4_1_mux1_2_s), .A(n4_1_mux1_1_s), .B(S_2), .S(n2_1_mux1_1_s));
  _2_1_Mux1 u_2_1_mux1_2 (.S_0(n2_1_mux1_3_s), .A(n2_1_mux1_1_s), .B(S_3), .S(n2_1_mux1_2_s));
  _4_1_Mux1 u_4_1_mux1_3 (.S_0(Input9), .S_1(Input10), .A(Input11), .B(Input12), .C(S_0), .D(S_1), .S(n4_1_mux1_3_s));
  _2_1_Mux1 u_2_1_mux1_3 (.S_0(n4_1_mux1_4_s), .A(n4_1_mux1_3_s), .B(S_2), .S(n2_1_mux1_3_s));
  _4_1_Mux1 u_4_1_mux1_4 (.S_0(Input13), .S_1(Input14), .A(Input15), .B(Input16), .C(S_0), .D(S_1), .S(n4_1_mux1_4_s));
  _2_1_Mux1 u_2_1_mux1_4 (.S_0(n2_1_mux1_6_s), .A(S_4), .B(n2_1_mux1_2_s), .S(n2_1_mux1_4_s));
  _4_1_Mux1 u_4_1_mux1_5 (.S_0(S_1), .S_1(S_0), .A(Input20), .B(Input19), .C(Input18), .D(Input17), .S(n4_1_mux1_5_s));
  _2_1_Mux1 u_2_1_mux1_5 (.S_0(S_2), .A(n4_1_mux1_6_s), .B(n4_1_mux1_5_s), .S(n2_1_mux1_5_s));
  _4_1_Mux1 u_4_1_mux1_6 (.S_0(S_1), .S_1(S_0), .A(Input24), .B(Input23), .C(Input22), .D(Input21), .S(n4_1_mux1_6_s));
  _2_1_Mux1 u_2_1_mux1_6 (.S_0(S_3), .A(n2_1_mux1_7_s), .B(n2_1_mux1_5_s), .S(n2_1_mux1_6_s));
  _4_1_Mux1 u_4_1_mux1_7 (.S_0(S_1), .S_1(S_0), .A(Input28), .B(Input27), .C(Input26), .D(Input25), .S(n4_1_mux1_7_s));
  _2_1_Mux1 u_2_1_mux1_7 (.S_0(S_2), .A(n4_1_mux1_8_s), .B(n4_1_mux1_7_s), .S(n2_1_mux1_7_s));
  _4_1_Mux1 u_4_1_mux1_8 (.S_0(S_1), .S_1(S_0), .A(Input32), .B(Input31), .C(Input30), .D(Input29), .S(n4_1_mux1_8_s));
endmodule
